// Logisim project 1KB .circ as structural Verilog: 5 circuits, main circuit main
module main (
  input  [7:0] INPUT,
  input  STORE,
  input  [9:0] ADDRESS,
  output [7:0] OUTPUT
);

  wire clock_1_out;
  wire [7:0] controlled_buffer_1_out;

  Clock clock_1 (.out(clock_1_out));
  assign controlled_buffer_1_out = STORE ? INPUT : 8'bz;  // Controlled_Buffer controlled_buffer_1
  _1KILO u_1kilo_1 (.CLK(clock_1_out), .INPUT(controlled_buffer_1_out), .ADDRESS(ADDRESS), .OUTPUT(OUTPUT));
endmodule

module _4BYTES (
  input  CLK,
  input  STORE,
  input  [1:0] ADDRESS,
  input  [7:0] INPUT,
  output [7:0] OUTPUT
);

  wire and_1_out, and_2_out, and_3_out, and_4_out, and_5_out, and_6_out, and_7_out, and_8_out, and_9_out,
       and_10_out, and_11_out, and_12_out, and_13_out, and_14_out, and_15_out, and_16_out, and_17_out,
       and_18_out, and_19_out, and_20_out, and_21_out, and_22_out, and_23_out, and_24_out, and_25_out,
       and_26_out, and_27_out, and_28_out, and_29_out, and_30_out, and_31_out, and_32_out, d_ff_1_q,
       d_ff_2_q, d_ff_3_q, d_ff_4_q, d_ff_5_q, d_ff_6_q, d_ff_7_q, d_ff_8_q, d_ff_9_q, d_ff_10_q, d_ff_11_q,
       d_ff_12_q, d_ff_13_q, d_ff_14_q, d_ff_15_q, d_ff_16_q, d_ff_17_q, d_ff_18_q, d_ff_19_q, d_ff_20_q,
       d_ff_21_q, d_ff_22_q, d_ff_23_q, d_ff_24_q, d_ff_25_q, d_ff_26_q, d_ff_27_q, d_ff_28_q, d_ff_29_q,
       d_ff_30_q, d_ff_31_q, d_ff_32_q, rw1, rw2, rw3, rw4;
  wire [7:0] controlled_buffer_1_out;

  assign controlled_buffer_1_out = STORE ? INPUT : 8'bz;  // Controlled_Buffer controlled_buffer_1
  and and_1 (and_1_out, rw1, d_ff_1_q);
  Decoder #(.select(2)) decoder_1 (.out0(rw1), .out1(rw2), .out2(rw3), .out3(rw4), .sel(ADDRESS));  // open: en
  and and_2 (and_2_out, rw2, d_ff_2_q);
  and and_3 (and_3_out, rw3, d_ff_3_q);
  and and_4 (and_4_out, rw1, d_ff_5_q);
  and and_5 (and_5_out, rw4, d_ff_4_q);
  and and_6 (and_6_out, rw2, d_ff_6_q);
  and and_7 (and_7_out, rw3, d_ff_7_q);
  D_Flip_Flop d_ff_1 (.clk(CLK), .D(controlled_buffer_1_out[7]), .Q(d_ff_1_q), .en(rw1));  // open: Qn, preset, reset
  D_Flip_Flop d_ff_2 (.clk(CLK), .D(controlled_buffer_1_out[7]), .Q(d_ff_2_q), .en(rw2));  // open: Qn, preset, reset
  D_Flip_Flop d_ff_3 (.clk(CLK), .D(controlled_buffer_1_out[7]), .Q(d_ff_3_q), .en(rw3));  // open: Qn, preset, reset
  D_Flip_Flop d_ff_4 (.clk(CLK), .D(controlled_buffer_1_out[7]), .Q(d_ff_4_q), .en(rw4));  // open: Qn, preset, reset
  or or_1 (OUTPUT[7], and_1_out, and_2_out, and_3_out, and_5_out);
  and and_8 (and_8_out, rw1, d_ff_9_q);
  and and_9 (and_9_out, rw4, d_ff_8_q);
  or or_2 (OUTPUT[6], and_4_out, and_6_out, and_7_out, and_9_out);
  and and_10 (and_10_out, rw2, d_ff_10_q);
  and and_11 (and_11_out, rw3, d_ff_11_q);
  D_Flip_Flop d_ff_5 (.clk(CLK), .D(controlled_buffer_1_out[6]), .Q(d_ff_5_q), .en(rw1));  // open: Qn, preset, reset
  D_Flip_Flop d_ff_6 (.clk(CLK), .D(controlled_buffer_1_out[6]), .Q(d_ff_6_q), .en(rw2));  // open: Qn, preset, reset
  D_Flip_Flop d_ff_7 (.clk(CLK), .D(controlled_buffer_1_out[6]), .Q(d_ff_7_q), .en(rw3));  // open: Qn, preset, reset
  D_Flip_Flop d_ff_8 (.clk(CLK), .D(controlled_buffer_1_out[6]), .Q(d_ff_8_q), .en(rw4));  // open: Qn, preset, reset
  and and_12 (and_12_out, rw1, d_ff_13_q);
  and and_13 (and_13_out, rw2, d_ff_14_q);
  and and_14 (and_14_out, rw4, d_ff_12_q);
  D_Flip_Flop d_ff_9 (.clk(CLK), .D(controlled_buffer_1_out[5]), .Q(d_ff_9_q));  // open: Qn, preset, en, reset
  D_Flip_Flop d_ff_10 (.clk(CLK), .D(controlled_buffer_1_out[5]), .Q(d_ff_10_q), .en(rw2));  // open: Qn, preset, reset
  D_Flip_Flop d_ff_11 (.clk(CLK), .D(controlled_buffer_1_out[5]), .Q(d_ff_11_q), .en(rw3));  // open: Qn, preset, reset
  D_Flip_Flop d_ff_12 (.clk(CLK), .D(controlled_buffer_1_out[5]), .Q(d_ff_12_q), .en(rw4));  // open: Qn, preset, reset
  or or_3 (OUTPUT[5], and_8_out, and_10_out, and_11_out, and_14_out);
  and and_15 (and_15_out, rw3, d_ff_15_q);
  and and_16 (and_16_out, rw4, d_ff_16_q);
  or or_4 (OUTPUT[4], and_12_out, and_13_out, and_15_out, and_16_out);
  D_Flip_Flop d_ff_13 (.clk(CLK), .D(controlled_buffer_1_out[4]), .Q(d_ff_13_q), .en(rw1));  // open: Qn, preset, reset
  D_Flip_Flop d_ff_14 (.clk(CLK), .D(controlled_buffer_1_out[4]), .Q(d_ff_14_q), .en(rw2));  // open: Qn, preset, reset
  D_Flip_Flop d_ff_15 (.clk(CLK), .D(controlled_buffer_1_out[4]), .Q(d_ff_15_q), .en(rw3));  // open: Qn, preset, reset
  D_Flip_Flop d_ff_16 (.clk(CLK), .D(controlled_buffer_1_out[4]), .Q(d_ff_16_q), .en(rw4));  // open: Qn, preset, reset
  or or_5 (OUTPUT[3], and_17_out, and_18_out, and_19_out, and_20_out);
  D_Flip_Flop d_ff_17 (.clk(CLK), .D(controlled_buffer_1_out[3]), .Q(d_ff_17_q), .en(rw1));  // open: Qn, preset, reset
  D_Flip_Flop d_ff_18 (.clk(CLK), .D(controlled_buffer_1_out[3]), .Q(d_ff_18_q), .en(rw2));  // open: Qn, preset, reset
  D_Flip_Flop d_ff_19 (.clk(CLK), .D(controlled_buffer_1_out[3]), .Q(d_ff_19_q), .en(rw3));  // open: Qn, preset, reset
  D_Flip_Flop d_ff_20 (.clk(CLK), .D(controlled_buffer_1_out[3]), .Q(d_ff_20_q), .en(rw4));  // open: Qn, preset, reset
  and and_17 (and_17_out, rw1, d_ff_17_q);
  D_Flip_Flop d_ff_21 (.clk(CLK), .D(controlled_buffer_1_out[2]), .Q(d_ff_21_q), .en(rw1));  // open: Qn, preset, reset
  D_Flip_Flop d_ff_22 (.clk(CLK), .D(controlled_buffer_1_out[2]), .Q(d_ff_22_q), .en(rw2));  // open: Qn, preset, reset
  D_Flip_Flop d_ff_23 (.clk(CLK), .D(controlled_buffer_1_out[2]), .Q(d_ff_23_q), .en(rw3));  // open: Qn, preset, reset
  D_Flip_Flop d_ff_24 (.clk(CLK), .D(controlled_buffer_1_out[2]), .Q(d_ff_24_q), .en(rw4));  // open: Qn, preset, reset
  or or_6 (OUTPUT[2], and_21_out, and_22_out, and_23_out, and_24_out);
  and and_18 (and_18_out, rw2, d_ff_18_q);
  and and_19 (and_19_out, rw3, d_ff_19_q);
  or or_7 (OUTPUT[1], and_25_out, and_26_out, and_27_out, and_28_out);
  and and_20 (and_20_out, rw4, d_ff_20_q);
  D_Flip_Flop d_ff_25 (.clk(CLK), .D(controlled_buffer_1_out[1]), .Q(d_ff_25_q), .en(rw1));  // open: Qn, preset, reset
  D_Flip_Flop d_ff_26 (.clk(CLK), .D(controlled_buffer_1_out[1]), .Q(d_ff_26_q), .en(rw2));  // open: Qn, preset, reset
  D_Flip_Flop d_ff_27 (.clk(CLK), .D(controlled_buffer_1_out[1]), .Q(d_ff_27_q), .en(rw3));  // open: Qn, preset, reset
  D_Flip_Flop d_ff_28 (.clk(CLK), .D(controlled_buffer_1_out[1]), .Q(d_ff_28_q), .en(rw4));  // open: Qn, preset, reset
  and and_21 (and_21_out, rw1, d_ff_21_q);
  and and_22 (and_22_out, rw2, d_ff_22_q);
  D_Flip_Flop d_ff_29 (.clk(CLK), .D(controlled_buffer_1_out[0]), .Q(d_ff_29_q), .en(rw1));  // open: Qn, preset, reset
  D_Flip_Flop d_ff_30 (.clk(CLK), .D(controlled_buffer_1_out[0]), .Q(d_ff_30_q), .en(rw2));  // open: Qn, preset, reset
  D_Flip_Flop d_ff_31 (.clk(CLK), .D(controlled_buffer_1_out[0]), .Q(d_ff_31_q), .en(rw3));  // open: Qn, preset, reset
  D_Flip_Flop d_ff_32 (.clk(CLK), .D(controlled_buffer_1_out[0]), .Q(d_ff_32_q), .en(rw4));  // open: Qn, preset, reset
  or or_8 (OUTPUT[0], and_29_out, and_30_out, and_31_out, and_32_out);
  and and_23 (and_23_out, rw3, d_ff_23_q);
  and and_24 (and_24_out, rw4, d_ff_24_q);
  and and_25 (and_25_out, rw1, d_ff_25_q);
  and and_26 (and_26_out, rw2, d_ff_26_q);
  and and_27 (and_27_out, rw3, d_ff_27_q);
  and and_28 (and_28_out, rw4, d_ff_28_q);
  and and_29 (and_29_out, rw1, d_ff_29_q);
  and and_30 (and_30_out, rw2, d_ff_30_q);
  and and_31 (and_31_out, rw3, d_ff_31_q);
  and and_32 (and_32_out, rw4, d_ff_32_q);

  // Other names for the same wires on the sheet: IE = STORE; OUT[7:0] = OUTPUT
endmodule

module _32BYTES (
  input  CLK,
  input  STORE,
  input  [4:0] ADDRESS,
  input  [7:0] INPUT,
  output [7:0] OUTPUT
);

  wire decoder_1_out0, decoder_1_out1, decoder_1_out2, decoder_1_out3, decoder_1_out4, decoder_1_out5,
       decoder_1_out6, decoder_1_out7;
  wire [7:0] controlled_buffer_1_out, n4bytes_1_output, n4bytes_2_output, n4bytes_3_output, n4bytes_4_output,
       n4bytes_5_output, n4bytes_6_output, n4bytes_7_output, n4bytes_8_output;

  assign controlled_buffer_1_out = STORE ? INPUT : 8'bz;  // Controlled_Buffer controlled_buffer_1
  Decoder #(.select(3)) decoder_1 (
    .out0(decoder_1_out0), .out1(decoder_1_out1), .out2(decoder_1_out2), .out3(decoder_1_out3),
    .out4(decoder_1_out4), .out5(decoder_1_out5), .out6(decoder_1_out6), .out7(decoder_1_out7),
    .sel(ADDRESS[4:2]));  // open: en
  _4BYTES u_4bytes_1 (
    .CLK(CLK), .STORE(decoder_1_out0), .ADDRESS(ADDRESS[1:0]), .INPUT(controlled_buffer_1_out),
    .OUTPUT(n4bytes_1_output));
  _4BYTES u_4bytes_2 (
    .CLK(CLK), .STORE(decoder_1_out2), .ADDRESS(ADDRESS[1:0]), .INPUT(controlled_buffer_1_out),
    .OUTPUT(n4bytes_2_output));
  _4BYTES u_4bytes_3 (
    .CLK(CLK), .STORE(decoder_1_out4), .ADDRESS(ADDRESS[1:0]), .INPUT(controlled_buffer_1_out),
    .OUTPUT(n4bytes_3_output));
  _4BYTES u_4bytes_4 (
    .CLK(CLK), .STORE(decoder_1_out6), .ADDRESS(ADDRESS[1:0]), .INPUT(controlled_buffer_1_out),
    .OUTPUT(n4bytes_4_output));
  _4BYTES u_4bytes_5 (
    .CLK(CLK), .STORE(decoder_1_out1), .ADDRESS(ADDRESS[1:0]), .INPUT(controlled_buffer_1_out),
    .OUTPUT(n4bytes_5_output));
  _4BYTES u_4bytes_6 (
    .CLK(CLK), .STORE(decoder_1_out3), .ADDRESS(ADDRESS[1:0]), .INPUT(controlled_buffer_1_out),
    .OUTPUT(n4bytes_6_output));
  _4BYTES u_4bytes_7 (
    .CLK(CLK), .STORE(decoder_1_out5), .ADDRESS(ADDRESS[1:0]), .INPUT(controlled_buffer_1_out),
    .OUTPUT(n4bytes_7_output));
  _4BYTES u_4bytes_8 (
    .CLK(CLK), .STORE(decoder_1_out7), .ADDRESS(ADDRESS[1:0]), .INPUT(controlled_buffer_1_out),
    .OUTPUT(n4bytes_8_output));
  Pull_Resistor pull_resistor_1 (.node(n4bytes_1_output));
  Pull_Resistor pull_resistor_2 (.node(n4bytes_5_output));
  Pull_Resistor pull_resistor_3 (.node(n4bytes_2_output));
  Pull_Resistor pull_resistor_4 (.node(n4bytes_6_output));
  Pull_Resistor pull_resistor_5 (.node(n4bytes_7_output));
  Pull_Resistor pull_resistor_6 (.node(n4bytes_3_output));
  Pull_Resistor pull_resistor_7 (.node(n4bytes_4_output));
  Pull_Resistor pull_resistor_8 (.node(n4bytes_8_output));
  assign OUTPUT = n4bytes_1_output | n4bytes_5_output | n4bytes_2_output | n4bytes_6_output | n4bytes_3_output | n4bytes_7_output | n4bytes_4_output | n4bytes_8_output;  // OR_Gate or_1, 8 bits wide
endmodule

module _256BYTES (
  input  CLK,
  input  [7:0] INPUT,
  input  STORE,
  input  [7:0] ADDRESS,
  output [7:0] OUTPUT
);

  wire decoder_1_out0, decoder_1_out1, decoder_1_out2, decoder_1_out3, decoder_1_out4, decoder_1_out5,
       decoder_1_out6, decoder_1_out7;
  wire [7:0] controlled_buffer_1_out, n32bytes_1_output, n32bytes_2_output, n32bytes_3_output,
       n32bytes_4_output, n32bytes_5_output, n32bytes_6_output, n32bytes_7_output, n32bytes_8_output;

  assign controlled_buffer_1_out = STORE ? INPUT : 8'bz;  // Controlled_Buffer controlled_buffer_1
  Decoder #(.select(3)) decoder_1 (
    .out0(decoder_1_out0), .out1(decoder_1_out1), .out2(decoder_1_out2), .out3(decoder_1_out3),
    .out4(decoder_1_out4), .out5(decoder_1_out5), .out6(decoder_1_out6), .out7(decoder_1_out7),
    .sel(ADDRESS[7:5]));  // open: en
  _32BYTES u_32bytes_1 (
    .CLK(CLK), .ADDRESS(ADDRESS[4:0]), .INPUT(controlled_buffer_1_out), .STORE(decoder_1_out0),
    .OUTPUT(n32bytes_1_output));
  _32BYTES u_32bytes_2 (
    .CLK(CLK), .ADDRESS(ADDRESS[4:0]), .INPUT(controlled_buffer_1_out), .STORE(decoder_1_out2),
    .OUTPUT(n32bytes_2_output));
  _32BYTES u_32bytes_3 (
    .CLK(CLK), .ADDRESS(ADDRESS[4:0]), .INPUT(controlled_buffer_1_out), .STORE(decoder_1_out4),
    .OUTPUT(n32bytes_3_output));
  _32BYTES u_32bytes_4 (
    .CLK(CLK), .ADDRESS(ADDRESS[4:0]), .INPUT(controlled_buffer_1_out), .STORE(decoder_1_out6),
    .OUTPUT(n32bytes_4_output));
  _32BYTES u_32bytes_5 (
    .CLK(CLK), .ADDRESS(ADDRESS[4:0]), .INPUT(controlled_buffer_1_out), .STORE(decoder_1_out1),
    .OUTPUT(n32bytes_5_output));
  _32BYTES u_32bytes_6 (
    .CLK(CLK), .ADDRESS(ADDRESS[4:0]), .INPUT(controlled_buffer_1_out), .STORE(decoder_1_out3),
    .OUTPUT(n32bytes_6_output));
  _32BYTES u_32bytes_7 (
    .CLK(CLK), .ADDRESS(ADDRESS[4:0]), .INPUT(controlled_buffer_1_out), .STORE(decoder_1_out5),
    .OUTPUT(n32bytes_7_output));
  _32BYTES u_32bytes_8 (
    .CLK(CLK), .ADDRESS(ADDRESS[4:0]), .INPUT(controlled_buffer_1_out), .STORE(decoder_1_out7),
    .OUTPUT(n32bytes_8_output));
  assign OUTPUT = n32bytes_1_output | n32bytes_5_output | n32bytes_2_output | n32bytes_6_output | n32bytes_3_output | n32bytes_7_output | n32bytes_4_output | n32bytes_8_output;  // OR_Gate or_1, 8 bits wide
endmodule

module _1KILO (
  input  CLK,
  input  [7:0] INPUT,
  input  [9:0] ADDRESS,
  output [7:0] OUTPUT
);

  wire decoder_1_out0, decoder_1_out1, decoder_1_out2, decoder_1_out3;
  wire [7:0] n256bytes_1_output, n256bytes_2_output, n256bytes_3_output, n256bytes_4_output;

  Decoder #(.select(2)) decoder_1 (
    .out0(decoder_1_out0), .out1(decoder_1_out1), .out2(decoder_1_out2), .out3(decoder_1_out3),
    .sel(ADDRESS[9:8]));  // open: en
  _256BYTES u_256bytes_1 (
    .CLK(CLK), .INPUT(INPUT), .ADDRESS(ADDRESS[7:0]), .STORE(decoder_1_out0), .OUTPUT(n256bytes_1_output));
  _256BYTES u_256bytes_2 (
    .CLK(CLK), .INPUT(INPUT), .ADDRESS(ADDRESS[7:0]), .STORE(decoder_1_out1), .OUTPUT(n256bytes_2_output));
  _256BYTES u_256bytes_3 (
    .CLK(CLK), .INPUT(INPUT), .ADDRESS(ADDRESS[7:0]), .STORE(decoder_1_out2), .OUTPUT(n256bytes_3_output));
  _256BYTES u_256bytes_4 (
    .CLK(CLK), .INPUT(INPUT), .ADDRESS(ADDRESS[7:0]), .STORE(decoder_1_out3), .OUTPUT(n256bytes_4_output));
  assign OUTPUT = n256bytes_1_output | n256bytes_2_output | n256bytes_3_output | n256bytes_4_output;  // OR_Gate or_1, 8 bits wide
endmodule
